# Fritzing sketch Water_Quality_Diagram (saved by Fritzing 0.9.3b)
breadboards: 1

parts:
  Boron1 = Particle Boron
  Part1 = PowerBoost 500 Charger
  Part2 = Arduino Uno (Rev3) - ICSP

nets:
  N1: Boron1.RESET, Part2.RESET
  N2: Boron1.3.3V, Part1.VBAT_OUT
  N3: Boron1.MD, Part2.GND
  N4: Boron1.SDA, Part2.A4/SDA
  N5: Boron1.SCL, Part2.A5/SCL
  N6: Part1.5.0V, Part2.5V

custom parts:
  Particle Boron: The Boron LTE is a powerful LTE CAT-M1 enabled development kit that can act as either a standalone cellular device or LTE enabled gateway, repeater, or endpoint for a Particle Mesh networks. Equipped with the Nordic nRF52840 and u-blox SARA 410 processors, the Boron has built-in battery charging circuitry which makes it easier to connect a Li-Po battery and 20 mixed signal GPIOs to interface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
